// Logisim project mapa2.circ as structural Verilog: 3 circuits, main circuit main
module main (
  input  [3:0] _0,
  input  [3:0] _1,
  input  [3:0] _2,
  input  [3:0] _3,
  input  [3:0] _4,
  input  [3:0] _5,
  input  [3:0] _6,
  input  [3:0] _7,
  input  [3:0] _8,
  input  [3:0] _9,
  input  [3:0] _10,
  input  [3:0] _11,
  input  [3:0] _12,
  input  [3:0] _13,
  input  [3:0] _14,
  input  [3:0] \input ,
  input  [3:0] _15
);

  wire LogicaEstados_a, LogicaEstados_b, LogicaEstados_c, LogicaEstados_d, LogicaEstados_minus_a,
       LogicaEstados_minus_b, LogicaEstados_minus_c, LogicaEstados_minus_d, LogicaSalida_sa, LogicaSalida_sb,
       LogicaSalida_sc, LogicaSalida_sd, LogicaSalida_se, LogicaSalida_sf, LogicaSalida_sg;

  Multiplexer #(.select(4), .width(4)) multiplexer_1 (
    .in0(_0), .in1(_1), .in2(_2), .in3(_3), .in4(_4), .in5(_5), .in6(_6), .in7(_7), .in8(_8), .in9(_9),
    .in10(_10), .in11(_11), .in12(_12), .in13(_13), .in14(_14), .in15(_15), .sel(\input ));  // open: out, en
  LogicaEstados LogicaEstados (
    .A(LogicaEstados_a), .minus_A(LogicaEstados_minus_a), .B(LogicaEstados_b),
    .minus_B(LogicaEstados_minus_b), .C(LogicaEstados_c), .minus_C(LogicaEstados_minus_c),
    .D(LogicaEstados_d), .minus_D(LogicaEstados_minus_d));
  LogicaSalida LogicaSalida (
    .A(LogicaEstados_a), .minus_A(LogicaEstados_minus_a), .B(LogicaEstados_b),
    .minus_B(LogicaEstados_minus_b), .Sa(LogicaSalida_sa), .C(LogicaEstados_c),
    .minus_C(LogicaEstados_minus_c), .D(LogicaEstados_d), .minus_D(LogicaEstados_minus_d),
    .Sb(LogicaSalida_sb), .Sc(LogicaSalida_sc), .Sd(LogicaSalida_sd), .Se(LogicaSalida_se),
    .Sf(LogicaSalida_sf), .Sg(LogicaSalida_sg));
  _7_Segment_Display u_7_segment_display_1 (
    .g(LogicaSalida_sg), .f(LogicaSalida_sf), .a(LogicaSalida_sa), .b(LogicaSalida_sb), .e(LogicaSalida_se),
    .d(LogicaSalida_sd), .c(LogicaSalida_sc));  // open: dp
endmodule

module LogicaEstados (
  output A,
  output minus_A,
  output B,
  output minus_B,
  output C,
  output minus_C,
  output D,
  output minus_D
);

  wire AD_out, BC_out, BCD_out, BD_BC_out, BD_out, CD_out, clock_1_out, minus_A_B__C_A_out,
       minus_A_B_C_A_out, minus_A_B_out, minus_AB__BD_out, minus_AB_out, minus_AC_CD_out, minus_AC_out,
       minus_BD_out;

  Clock clock_1 (.out(clock_1_out));
  J_K_Flip_Flop u_A (.J(BD_BC_out), .clk(clock_1_out), .K(BCD_out), .Q(A), .Qn(minus_A));  // open: preset, en, reset
  J_K_Flip_Flop u_B (.J(D), .clk(clock_1_out), .K(minus_AC_CD_out), .Q(B), .Qn(minus_B));  // open: preset, en, reset
  J_K_Flip_Flop u_C (
    .J(AD_out), .clk(clock_1_out), .K(minus_AB__BD_out), .Q(C), .Qn(minus_C));  // open: preset, en, reset
  J_K_Flip_Flop u_D (
    .J(minus_A_B__C_A_out), .clk(clock_1_out), .K(minus_A_B_C_A_out), .Q(D), .Qn(minus_D));  // open: preset, en, reset
  and BC (BC_out, B, C);
  and BCD (BCD_out, B, C, D);
  and BD (BD_out, B, D);
  and AD (AD_out, A, D);
  and CD (CD_out, C, D);
  and minus_AC (minus_AC_out, minus_A, C);
  and minus_AB (minus_AB_out, minus_A, B);
  and minus_BD (minus_BD_out, minus_B, D);
  and minus_A_B (minus_A_B_out, minus_A, minus_B);
  or BD_BC (BD_BC_out, BC_out, BD_out);
  or minus_AC_CD (minus_AC_CD_out, CD_out, minus_AC_out);
  or minus_AB__BD (minus_AB__BD_out, minus_AB_out, minus_BD_out);
  or minus_A_B_C_A (minus_A_B_C_A_out, minus_A_B_out, C, A);
  or minus_A_B__C_A (minus_A_B__C_A_out, minus_A_B_out, minus_C, A);
endmodule

module LogicaSalida (
  input  A,
  input  minus_A,
  input  B,
  input  minus_B,
  input  C,
  input  minus_C,
  input  D,
  input  minus_D,
  output Sa,
  output Sb,
  output Sc,
  output Sd,
  output Se,
  output Sf,
  output Sg
);

  wire A_B_C_out, A_D_out, AB_out, AD_out, B_D_out, BC_out, BD_out, minus_A_B_C_out, minus_A_B_out,
       minus_A_BCD_out, minus_A_BD_2_out, minus_A_BD_out, minus_A_C_D_out, minus_B_C_D_out, minus_B_C_out,
       minus_BCD_out, minus_C_D_out, minus_CB_out, minus_DAC_out, minus_DC_out;

  and minus_C_D (minus_C_D_out, minus_D, minus_C);
  and minus_A_B (minus_A_B_out, minus_A, minus_B);
  and minus_BCD (minus_BCD_out, C, minus_B, D);
  and minus_CB (minus_CB_out, B, minus_C);
  and AB (AB_out, A, B);
  and minus_A_B_C (minus_A_B_C_out, minus_A_B_out, minus_C);
  and BD (BD_out, D, B);
  and AD (AD_out, A, D);
  and minus_DC (minus_DC_out, C, minus_D);
  and minus_A_C_D (minus_A_C_D_out, minus_C, minus_A, minus_D);
  and A_B_C (A_B_C_out, minus_C, A, minus_B);
  and minus_A_BCD (minus_A_BCD_out, minus_A_B_out, C, D);
  and minus_DAC (minus_DAC_out, A, C, minus_D);
  and minus_B_C_D (minus_B_C_D_out, minus_B, minus_C, minus_D);
  and A_D (A_D_out, minus_D, A);
  and minus_A_BD (minus_A_BD_out, minus_A_B_out, D);
  and BC (BC_out, C, B);
  and B_D (B_D_out, B, minus_D);
  and minus_A_BD_2 (minus_A_BD_2_out, minus_A_B_out, D);
  and minus_B_C (minus_B_C_out, minus_B, minus_C);
  or minus_C_D____CB____BCD (Sa, A, minus_C_D_out, minus_BCD_out, minus_CB_out);
  or minus_A_B_C___BD___AD___AB____DC (Sb, AB_out, minus_A_B_C_out, BD_out, AD_out, minus_DC_out);
  or B_A_D_C (Sc, D, A, B, C);
  or minus_A_C_D____A_B_C____A_BCD____DAC (Sd, minus_A_C_D_out, A_B_C_out, minus_A_BCD_out, minus_DAC_out);
  or minus_DAC____B_C_D (Se, minus_DAC_out, minus_B_C_D_out);
  or A_D___A_BD___BC___B_D (Sf, A_D_out, minus_A_BD_out, BC_out, B_D_out);
  or A_D____C_D____B_C___BC____A_BD (Sg, A_D_out, BC_out, minus_A_BD_2_out, minus_C_D_out, minus_B_C_out);
endmodule
